# Fritzing sketch fake-eastron-and-modbus-bridge (saved by Fritzing 0.9.5d)
circuit board: 8.46667cm x 5.64444cm

parts:
  A1 = Esp32-c3 super mini
  U3 = Mini-360 DC-DC Buck converter [package=THT]
  M1 = MAX485 Breakout [package=THT]
  M2 = MAX485 Breakout [package=THT]
  A2 = Current transformer PZCT02
  A3 = Current transformer PZCT02
  A4 = Current transformer PZCT02
  R1 = Resistor [tolerance=±0.5% resistance=50 package=THT]
  R2 = Resistor [tolerance=±0.5% resistance=50 package=THT]
  R3 = Resistor [tolerance=±0.5% resistance=50 package=THT]
  M3 = MAX485 Breakout [package=THT]
  R5 = Resistor [tolerance=±0.5% resistance=1200 package=THT]
  R6 = Resistor [tolerance=±0.5% resistance=330 package=THT]

nets (from the breadboard view):
  N1: A1.Pin_6, A3.Pin_2, R1.Pin_1
  N2: A1.Pin_7, A2.Pin_2, R2.Pin_1
  N3: A1.Pin_8, A4.Pin_2, R3.Pin_1
  N4: A1.Pin_9, M2.DI
  N5: A1.Pin_10, M2.RO
  N6: A1.Pin_11, M3.DI
  N7: A1.Pin_12, M3.RO
  N8: A1.Pin_13, M1.DI
  N9: A1.Pin_14, M1.RO
  VCC: U3.OUT+, M1.VCC, M2.VCC, M3.VCC, R5.Pin_1
  N10: U3.OUT-, R6.Pin_0
  N11: A4.Pin_1, R3.Pin_0, R5.Pin_0

notes:
  Deye inverter 12 Vdc at port CN2 Pins 7+ and 8- (RSD) up to 100 mA current
  Deye ModeBUS port
  Colors with RJ45 568A plug
  Deye (external) Meter-485 port
  Colors with RJ45 586A plug
  Deye BMS port (RS485 wires)
  CAN uses middle wires (blue)
  Split core current transformers
  with 3000:1 ratio or less

custom parts:
  Esp32-c3 super mini: ESP32-C3 Development Board ESP32 SuperMini Development Board ESP32 Development Board WiFi Bluetooth.
  Mini-360 DC-DC Buck converter: Mini-360 DC-DC Buck converter. Tiny buck step down voltage converter, input voltage 4.75 to 23V output 1 to 17V adjustable. Available from ebay and the like.
  MAX485 Breakout: MAX485 RS485 breakout board
  Current transformer PZCT02: Current transformer PZCT02.
